# Fritzing sketch Sketch-Receiver board (saved by Fritzing 0.9.6b)
breadboards: 1

parts:
  Composant1 = Arduino Uno (Rev3) - ICSP
  U1 = LCD-16X2 [package=lcd-16x2]
  R1 = Trimmer Potentiometer [maximum_resistance=10kΩ package=THT]
  R2 = Resistor [tolerance=±5% power=0.25 resistance=220 package=THT]
  U2 = RF-LINK_RX [package=rf-link_rx]
  ANT1 = Antenna
  ZS-042_RTC1 = ZS-042 RTC Module
  R3 = Resistor [tolerance=±5% power=0.25 resistance=220 package=THT]  # not connected

nets:
  GND: Composant1.GND, U1.VSS, U1.R_W, U1.K, R1.leg1, U2.GND, ZS-042_RTC1.GND
  N1: Composant1.D10_PWM/SS, U2.DATA
  N2: Composant1.D11_PWM/MOSI, U1.E
  N3: Composant1.D12/MISO, U1.RS
  N4: Composant1.A5/SCL, ZS-042_RTC1.SCL
  N5: Composant1.D2, U1.DB7
  N6: Composant1.D3_PWM, U1.DB6
  N7: Composant1.D4, U1.DB5
  N8: Composant1.D5_PWM, U1.DB4
  5V: Composant1.5V, U1.VDD, R1.leg2, R2.Pin_0, U2.+5V, ZS-042_RTC1.VCC
  N9: U1.VO, R1.wiper
  N10: U1.A, R2.Pin_1
  N11: U2.ANT, ANT1.antenna_lead
