# Fritzing sketch Sketch-Transmitter-board (saved by Fritzing 0.9.6b)
breadboards: 1

parts:
  Load_Cell1 = Load Cell - Red/white/black/green
  HX711-1 = HX711 Weighing Sensor Module
  Arduino_UNO = Arduino Uno (Rev3)
  RF-434Mhz = RF-LINK_TX [package=rf-link_tx]
  Load_Cell2 = Load Cell - Red/white/black/green
  Load_Cell3 = Load Cell - Red/white/black/green
  Load_Cell4 = Load Cell - Red/white/black/green
  HX711-2 = HX711 Weighing Sensor Module
  HX711-3 = HX711 Weighing Sensor Module
  HX711-4 = HX711 Weighing Sensor Module
  ANTENNA = Antenna
  SW1 = DIP Switch 8 Position [package=dipswitch-08]  # not connected
  Green_LED = LED - 3mm [color="Green (555nm)" current=0.030 package="3 mm [THT]"]
  DHT11 = DHT11 Humitidy and Temperature Sensor
  R5 = Resistor [tolerance=±5% resistance=1.5k package="0603 [SMD]"]

nets:
  N1: Load_Cell1.wire1, HX711-1.E+
  N2: Load_Cell1.wire2, HX711-1.A+
  N3: Load_Cell1.wire3, HX711-1.E-
  N4: Load_Cell1.wire4, HX711-1.A-
  VCC: HX711-1.VCC, Arduino_UNO.5V, RF-434Mhz.+5V, HX711-2.VCC, HX711-3.VCC, HX711-4.VCC, DHT11.VDD
  GND: HX711-1.GND, Arduino_UNO.A2, Arduino_UNO.GND, RF-434Mhz.GND, HX711-2.GND, HX711-3.GND, HX711-4.GND, Green_LED.anode, DHT11.GND
  N5: HX711-1.DO/RX, Arduino_UNO.D2
  N6: HX711-1.CK/TX, Arduino_UNO.D3_PWM
  N7: Arduino_UNO.D8, HX711-4.DO/RX
  N8: Arduino_UNO.D9_PWM, HX711-4.CK/TX
  N9: Arduino_UNO.D11_PWM/MOSI, Green_LED.cathode, R5.Pin_0, R5.Pin_1
  N10: Arduino_UNO.D12/MISO, RF-434Mhz.DATA
  N11: Arduino_UNO.D13/SCK, DHT11.DATA
  N12: Arduino_UNO.D4, HX711-2.DO/RX
  N13: Arduino_UNO.D5_PWM, HX711-2.CK/TX
  N14: Arduino_UNO.D6_PWM, HX711-3.DO/RX
  N15: Arduino_UNO.D7, HX711-3.CK/TX
  N16: RF-434Mhz.ANT, ANTENNA.antenna_lead
  N17: Load_Cell2.wire1, HX711-2.E+
  N18: Load_Cell2.wire2, HX711-2.A+
  N19: Load_Cell2.wire3, HX711-2.E-
  N20: Load_Cell2.wire4, HX711-2.A-
  N21: Load_Cell3.wire1, HX711-3.E+
  N22: Load_Cell3.wire2, HX711-3.A+
  N23: Load_Cell3.wire3, HX711-3.E-
  N24: Load_Cell3.wire4, HX711-3.A-
  N25: Load_Cell4.wire1, HX711-4.E+
  N26: Load_Cell4.wire2, HX711-4.A+
  N27: Load_Cell4.wire3, HX711-4.E-
  N28: Load_Cell4.wire4, HX711-4.A-

custom parts:
  Load Cell - Red/white/black/green: A rectangle load cell/weighting pressure Sensor with four wires - Red, white, black, green. Normally corresponding with E+, E-, A+, A- respectively.
  HX711 Weighing Sensor Module: HX711 is a precision 24-bit analog-to-digital converter (ADC) designed for weigh scales and industrial control applications to interface directly with a bridge sensor.
  DHT11 Humitidy and Temperature Sensor: DHT11 Humidity and Temperature Sensor
